// Digital circuit Menor.dig as structural Verilog
module Menor (
  input  [3:0] In1,
  input  [3:0] In2,
  output [3:0] Menor
);

  wire comparator_1_lt;

  Comparator #(.Bits(4)) comparator_1 (.a(In1), .b(In2), .lt(comparator_1_lt));  // open: gt, eq
  Multiplexer #(.Bits(4)) multiplexer_1 (.sel(comparator_1_lt), .in_0(In2), .in_1(In1), .out(Menor));
endmodule
