// Digital circuit SomaVetor.dig as structural Verilog
module SomaVetor (
  input  clk,
  output [3:0] out_2
);

  wire Compara, comparator_1_eq;
  wire [2:0] iterador, S_soma;
  wire [3:0] D_rom, sum_q;

  Register #(.Bits(4)) sum (.D(out_2), .C(clk), .en(Compara), .Q(sum_q));
  Register #(.Bits(3)) i (.D(S_soma), .C(clk), .en(Compara), .Q(iterador));
  Comparator #(.Bits(3)) comparator_1 (.a(iterador), .b(3'b111), .eq(comparator_1_eq));  // open: gt, lt
  Add #(.Bits(4)) add_1 (.a(D_rom), .b(sum_q), .c_i(1'b0), .s(out_2));  // open: c_o
  Add #(.Bits(3)) add_2 (.a(iterador), .b(3'b001), .c_i(1'b0), .s(S_soma));  // open: c_o
  not not_1 (Compara, comparator_1_eq);
  Seven_Seg_Hex seven_seg_hex_1 (.d(out_2), .dp(Compara));
  ROM #(.AddrBits(3), .Bits(4)) rom_1 (.A(iterador), .sel(1'b1), .D(D_rom));

  // Other names for the same wires on the sheet: D_soma[3:0] = out_2

  // Notes on the sheet:
  //   contents of rom_1 (hex, n*v repeats v):
  //   2,3,7,0,1,0,0,1
endmodule
