// Digital circuit comparadorSomador.dig as structural Verilog
module comparadorSomador (
  input  [3:0] a,
  input  [3:0] b,
  input  [3:0] c,
  output [3:0] out_4
);

  wire add_1_c_o, comparator_1_lt;
  wire [3:0] add_1_s, add_2_s, menor_1_menor, menor_2_menor, multiplexer_1_out;

  Menor menor_1 (.In1(b), .In2(c), .Menor(menor_1_menor));
  Menor menor_2 (.In1(a), .In2(c), .Menor(menor_2_menor));
  Comparator #(.Bits(4)) comparator_1 (.a(a), .b(b), .lt(comparator_1_lt));  // open: gt, eq
  Add #(.Bits(4)) add_1 (.a(a), .b(b), .c_i(1'b0), .s(add_1_s), .c_o(add_1_c_o));
  Add #(.Bits(4)) add_2 (.a(add_1_s), .b(c), .c_i(add_1_c_o), .s(add_2_s));  // open: c_o
  Multiplexer #(.Bits(4)) multiplexer_1 (
    .sel(comparator_1_lt), .in_0(menor_1_menor), .in_1(menor_2_menor), .out(multiplexer_1_out));
  Sub #(.Bits(4)) sub_1 (.a(add_2_s), .b(multiplexer_1_out), .c_i(1'b0), .s(out_4));  // open: c_o
endmodule
