// Logisim project letra_a.circ as structural Verilog: 1 circuit, main circuit main
module main (
  input  a,
  input  b,
  input  c,
  output s
);

  wire and_1_out, and_2_out;

  and and_1 (and_1_out, ~a, b, c);  // AND_Gate
  and and_2 (and_2_out, a, b);
  or or_1 (s, and_2_out, and_1_out);
endmodule
