// Digital circuit letra_a.dig as structural Verilog
module letra_a (
  input  a,
  input  b,
  input  c,
  output out_4
);

  wire and_1_out, and_2_out;

  and and_1 (and_1_out, b, a);
  and and_2 (and_2_out, ~a, b, c);  // And
  or or_1 (out_4, and_2_out, and_1_out);
endmodule
