// Digital circuit letra_c.dig as structural Verilog
module letra_c (
  input  a,
  input  b,
  input  c,
  output out_2
);

  wire and_1_out, and_2_out;

  and and_1 (and_1_out, a, b, c);
  and and_2 (and_2_out, a, b);
  or or_1 (out_2, and_1_out, and_2_out, a, b, c);
endmodule
